# Fritzing sketch CircuitSchematic (saved by Fritzing 0.9.3b)
breadboards: 1

parts:
  Raspberry_Pi_1 = Raspberry Pi 3 [part_number=RPI-3-V1.2]
  RE1 = Rotary Encoder [package=THT]
  M1 = DC Motor
  Power_plug1 = Power plug
  IC1 = L293D [package=THT]

nets:
  N1: Raspberry_Pi_1.GIPO21, IC1.Enable_2
  N2: Raspberry_Pi_1.GIPO20, IC1.In_3
  N3: Raspberry_Pi_1.GIPO16, IC1.In_4
  N4: Raspberry_Pi_1.GIPO18, RE1.EncoderPinB
  5V: Raspberry_Pi_1.5V, Power_plug1.VCC, IC1.0V, IC1.+Vmotor
  N5: RE1.EncoderPinA, Power_plug1.GND, IC1.+V
  N6: M1.pin_1, IC1.Out_4_(_Controlled_by_Enable_2_)
  N7: M1.pin_2, IC1.Out_3_(_Controlled_by_Enable_2_)
